# Fritzing sketch fritzing-schematic (saved by Fritzing 0.9.3b)

parts:
  Part1 = Arduino Mega 2560 (Rev3)
  DHT-22 = Humidity and Temperature Sensor RHT03
  R1 = Resistor [tolerance=±5% resistance=220 package="2512 [SMD]"]  # not connected
  4_Channel_Relay = 4 Channel Power Relay
  U6 = LCD-16X2 [package=lcd-16x2]
  LCD_I2V = LCM1602 IIC [part_number="LCM1602 IIC" chip_label="LCM1602 IIC" package="DIP (Dual Inline) [THT]"]
  U7 = Voltage Regulator [package=to220-adj]
  C1 = Capacitor Polarized [package=cpol-radial-10uf-25v]
  part = ESP8266 WiFi Module [part_number=ESP8266]
  C2 = Capacitor Polarized [package=cpol-radial-100uf-25v]

nets:
  N1: Part1.D21/SCL, LCD_I2V.SCL
  N2: Part1.D20/SDA, LCD_I2V.SDA
  N3: Part1.D19/RX1, part.TXD
  N4: Part1.D18/TX1, part.RXD
  GND: Part1.GND, DHT-22.GND_2, 4_Channel_Relay.GND, LCD_I2V.GND, U7.ADJ, C1.-, part.GND, C2.-
  N5: Part1.D13_PWM, 4_Channel_Relay.IN1
  N6: Part1.D12_PWM, 4_Channel_Relay.IN2
  N7: Part1.D11_PWM, 4_Channel_Relay.IN3
  N8: Part1.D10_PWM, 4_Channel_Relay.IN4
  VCC: Part1.5V, DHT-22.Vcc, 4_Channel_Relay.JD-VCC, LCD_I2V.VCC, U7.OUT, C2.+
  N9: Part1.D5_PWM, DHT-22.Data-signal
  VSS: U6.VSS, LCD_I2V.VSS
  VDD: U6.VDD, LCD_I2V.VDD
  N10: U6.VO, LCD_I2V.V0
  N11: U6.RS, LCD_I2V.RS
  N12: U6.R_W, LCD_I2V.RW
  N13: U6.E, LCD_I2V.E
  N14: U6.DB0, LCD_I2V.D0
  N15: U6.DB1, LCD_I2V.D1
  N16: U6.DB2, LCD_I2V.D2
  N17: U6.DB3, LCD_I2V.D3
  N18: U6.DB4, LCD_I2V.D4
  N19: U6.DB5, LCD_I2V.D5
  N20: U6.DB6, LCD_I2V.D6
  N21: U6.DB7, LCD_I2V.D7
  N22: U6.A, LCD_I2V.A
  N23: U6.K, LCD_I2V.K
  N24: U7.IN, C1.+, part.VCC, part.CH_PD

notes:
  There is no 4x20 LCD in fritzing, but it should be a 4x20 LCD connected using a LCD I2C connector.
  When connecting make sure the orientation is of the LCD -> I2C connector is correct!
  LM1117T-3.3
  5 -> 3.3v

custom parts:
  4 Channel Power Relay: A 4 channel power relay. The module operates at 5V.
  LCM1602 IIC: I2C-Module to use a 1602 or 2004 LCD on with the wire.h libory Serial LCD Modul
  ESP8266 WiFi Module: Generic WiFi Module based on the ESP8266 with onboard PCB antenna and UART communications
